# Fritzing sketch TRS-80-Arduino (saved by Fritzing 0.9.3b)
circuit board: 9cm x 8cm
breadboards: 1

parts:
  FET2 = 2N7000 FET N-Channel [part_number=2N7000 package=TO92]
  Part1 = Arduino Uno (Rev3)
  IC2 = IC, DIP package, 20 pins [chip_label=ATF16V8B]
  LED1 = LED - 5mm [color="Red (633nm)" package="5 mm [THT]"]
  S1 = Pushbutton [package="[THT]"]
  J1 = double row female pin header, 50 pins [form="♀ (female)"]
  R1 = Resistor [tolerance=±5% resistance=220 package=THT]

nets (from the breadboard view):
  N1: FET2.gate, IC2.pin14
  N2: FET2.drain, J1.pin22
  N3: FET2.source, Part1.GND, IC2.pin10, S1.Pin_3, S1.Pin_4, J1.pin26, J1.pin27, J1.pin28, J1.pin29, J1.pin30, J1.pin31, J1.pin32, J1.pin33, J1.pin34, J1.pin35, J1.pin36, J1.pin37, J1.pin38, J1.pin39, J1.pin40, J1.pin41, J1.pin42, J1.pin43, J1.pin44, J1.pin45, J1.pin46, J1.pin47, J1.pin48, J1.pin49, J1.pin50, R1.Pin_1
  N4: Part1.D8, IC2.pin13
  N5: Part1.D9_PWM, IC2.pin17, J1.pin17
  N6: Part1.D10_PWM/SS, LED1.anode
  N7: Part1.D11_PWM/MOSI, S1.Pin_1, S1.Pin_2
  N8: Part1.D0/RX, J1.pin1
  N9: Part1.D1/TX, J1.pin2
  N10: Part1.D2, J1.pin3
  N11: Part1.D3_PWM, J1.pin4
  N12: Part1.D4, J1.pin5
  N13: Part1.D5_PWM, J1.pin6
  N14: Part1.D6_PWM, J1.pin7
  N15: Part1.D7, J1.pin8
  N16: Part1.5V, IC2.pin20
  N17: IC2.pin2, J1.pin16
  N18: IC2.pin3, J1.pin15
  N19: IC2.pin4, J1.pin14
  N20: IC2.pin5, J1.pin13
  N21: IC2.pin6, J1.pin12
  N22: IC2.pin7, J1.pin11
  N23: IC2.pin8, J1.pin10
  N24: IC2.pin9, J1.pin9
  N25: IC2.pin18, J1.pin18
  N26: IC2.pin19, J1.pin23, J1.pin24, J1.pin25
  N27: LED1.cathode, R1.Pin_0

notes:
  49 47 45 43 41 39 37 35 33 31 29 27 25 23 21 19 17 15 13 11  9  7  5  3  1
  RESET*
  IOWAIT*
  50 48 46 44 42 40 38 36 34 32 30 28 26 24 22 20 18 16 14 12 10  8  6  4  2
  M1*
  ----------------------------------- GND -----------------------------------
  * = Active Low
  NC
  A7 A6 A5 A4 A3 A2 A1 A0 D7 D6 D5 D4 D3 D2 D1 D0
  OUT*
  EXTIOSEL*
  IN*
  IOREQ*
  IOINT*
  2N7000
  ATF16V8B

custom parts:
  2N7000 FET N-Channel: A 2N7000 MOSFET N-Channel Transistor
